# Fritzing sketch cablagekeyboxI2C (saved by Fritzing 0.9.3b)
breadboards: 1

parts:
  Raspberry_Pi_Zero2 = Raspberry Pi Zero
  R4 = Resistor [tolerance=±5% resistance=220 package=THT]
  S3 = Pushbutton [package="[THT]"]
  S4 = Pushbutton [package="[THT]"]
  Grove2 = Grove OLED 128x96
  R5 = Resistor [tolerance=±5% resistance=220 package=THT]

nets:
  3V3: Raspberry_Pi_Zero2.3v3, Grove2.VCC
  N1: Raspberry_Pi_Zero2.GPIO2, Grove2.SDA
  N2: Raspberry_Pi_Zero2.GPIO3, Grove2.SCL
  N3: Raspberry_Pi_Zero2.GIPO19, R4.Pin_1, S4.Pin_3, S4.Pin_4
  N4: Raspberry_Pi_Zero2.GIPO18, S3.Pin_3, S3.Pin_4, R5.Pin_1
  GND: Raspberry_Pi_Zero2.GND, Grove2.GND
  N5: R4.Pin_0, R5.Pin_0
  N6: S3.Pin_1, S3.Pin_2, S4.Pin_1, S4.Pin_2
