# Fritzing sketch calblageKeyboxSPI (saved by Fritzing 0.9.3b)
breadboards: 1

parts:
  OLED1 = 128x64 Monochrom OLED Display with SPI Control
  R1 = Resistor [tolerance=±5% resistance=220 package=THT]
  S1 = Pushbutton [package="[THT]"]
  Raspberry_Pi_Zero1 = Raspberry Pi Zero
  S2 = Pushbutton [package="[THT]"]
  R2 = Resistor [tolerance=±5% resistance=220 package=THT]

nets:
  N1: OLED1.Data, Raspberry_Pi_Zero1.GPIO10
  N2: OLED1.Clock, Raspberry_Pi_Zero1.GPIO11
  N3: OLED1.SA0/DC, Raspberry_Pi_Zero1.GPIO23
  N4: OLED1.Reset, Raspberry_Pi_Zero1.GPIO24
  VIN: OLED1.Vin, S1.Pin_1, S1.Pin_2, Raspberry_Pi_Zero1.3v3, S2.Pin_1, S2.Pin_2
  GND: OLED1.GND, R1.Pin_0, Raspberry_Pi_Zero1.GPIO14, Raspberry_Pi_Zero1.GND, R2.Pin_0
  N5: R1.Pin_1, S1.Pin_3, S1.Pin_4, Raspberry_Pi_Zero1.GPIO18
  N6: Raspberry_Pi_Zero1.GPIO17, S2.Pin_3, S2.Pin_4, R2.Pin_1

notes:
  -Connect display ground to Raspberry Pi ground
  -Connect display VIN to Raspberry Pi 3.3 volt.
  -Connect display CS to Raspberry Pi CE0.
  -Connect display RST to Raspberry Pi GPIO 24.
  -Connect display DC to Raspberry Pi GPIO 23
  -Connect display CLK to Raspberry Pi SCLK
  -Connect display Data to Raspberry Pi MOSI
