# Fritzing sketch cablagekeyboxI2C (saved by Fritzing 0.9.3b)
breadboards: 1

parts:
  Raspberry_Pi_Zero2 = Raspberry Pi Zero
  R3 = Resistor [tolerance=±5% resistance=220 package=THT]
  R4 = Resistor [tolerance=±5% resistance=220 package=THT]
  S3 = Pushbutton [package="[THT]"]
  S4 = Pushbutton [package="[THT]"]
  Grove2 = Grove OLED 128x96

nets:
  3V3: Raspberry_Pi_Zero2.3v3, Raspberry_Pi_Zero2.3V3, S3.Pin_1, S3.Pin_2, S4.Pin_1, S4.Pin_2
  N1: Raspberry_Pi_Zero2.GPIO19, R4.Pin_1, S4.Pin_3, S4.Pin_4
  N2: Raspberry_Pi_Zero2.GPIO21, Grove2.VCC
  N3: Raspberry_Pi_Zero2.GPIO20, Grove2.SDA
  N4: Raspberry_Pi_Zero2.GPIO16, Grove2.SCL
  GND: Raspberry_Pi_Zero2.GND, Raspberry_Pi_Zero2.GPIO14, R3.Pin_0, R4.Pin_0, Grove2.GND
  N5: Raspberry_Pi_Zero2.GPIO18, R3.Pin_1, S3.Pin_3, S3.Pin_4
